# Fritzing sketch Counting System (saved by Fritzing 0.9.3b)
breadboards: 1

parts:
  Raspberry_Pi1 = Raspberry Pi 3 [part_number=RPI-3-V1.2]
  J3 = male pin header, 4 pins [form="♂ (male)"]
  LED1 = smd LED [color="Green (570nm)" package="1206 [SMD]"]
  R3 = Resistor [tolerance=±5% resistance=220 package="2512 [SMD]"]
  Part1 = KY-008 Laser Transmitter Module [package="Breakout board"]

nets:
  N1: Raspberry_Pi1.GPIO4, J3.pin2
  N2: Raspberry_Pi1.GPIO26, R3.Pin_0
  N3: Raspberry_Pi1.GND, J3.pin3, LED1.cathode, Part1.-
  N4: Raspberry_Pi1.5V, J3.pin4, Part1.S
  N5: LED1.anode, R3.Pin_1

custom parts:
  KY-008 Laser Transmitter Module: Laser Transmitter module KY-008 for Arduino, emits a dot shaped red laser beam.
