# Fritzing sketch Delivery (saved by Fritzing 0.9.3b)

parts:
  J3 = male pin header, 13 pins [form="♂ (male)"]
  J4 = male pin header, 13 pins [form="♂ (male)"]
  U1 = RFID RC522 SIP - 8 pins [chip_label="RFID RC522" package="SIP (Single Inline) [THT]"]
  M1 = fc-51 [package=THT]

nets:
  N1: J3.pin2, U1.NSS
  N2: J3.pin3, U1.RST
  N3: J3.pin10, M1.pin1
  N4: J3.pin11, U1.GND
  N5: J3.pin13, M1.pin3
  N6: J4.pin2, U1.SCK
  N7: J4.pin3, U1.MISO
  N8: J4.pin4, U1.MOSI
  N9: J4.pin9, M1.pin2
  N10: J4.pin13, U1.VCC

custom parts:
  RFID RC522 SIP - 8 pins: A SIP stand-in part for RFID RC522 . With 8 pins on a 300 mil single inline package (SIP) footprint.
