# Fritzing sketch Environment Monitoring (saved by Fritzing 0.9.3b)
breadboards: 1

parts:
  Raspberry_Pi1 = Raspberry Pi 3 [part_number=RPI-3-V1.2]
  J2 = male pin header, 3 pins [form="♂ (male)"]
  J3 = male pin header, 4 pins [form="♂ (male)"]
  LED1 = smd LED [color="Red (633nm)" package="1206 [SMD]"]
  R3 = Resistor [tolerance=±5% resistance=220 package="2512 [SMD]"]

nets:
  N1: Raspberry_Pi1.GPIO2, J3.pin1
  N2: Raspberry_Pi1.GPIO3, J3.pin2
  N3: Raspberry_Pi1.GPIO4, J2.pin2
  N4: Raspberry_Pi1.GPIO26, R3.Pin_0
  N5: Raspberry_Pi1.GND, J2.pin1, J3.pin3, LED1.cathode
  N6: Raspberry_Pi1.5V, J2.pin3, J3.pin4
  N7: LED1.anode, R3.Pin_1
