# Fritzing sketch Packaging System (saved by Fritzing 0.9.3b)

parts:
  Raspberry_Pi_B_rev1 = Raspberry Pi 3 [part_number=RPI-3-V1.2]
  Part1 = HX711 Weighing Sensor Module
  U1 = RFID RC522 SIP - 8 pins [chip_label="RFID RC522" package="SIP (Single Inline) [THT]"]

nets:
  3V3: Raspberry_Pi_B_rev1.3v3, U1.VCC
  N1: Raspberry_Pi_B_rev1.GPIO10, Part1.VCC
  N2: Raspberry_Pi_B_rev1.GPIO9, U1.MOSI
  N3: Raspberry_Pi_B_rev1.GPIO11, U1.MISO
  GND: Raspberry_Pi_B_rev1.GND, U1.SCK, U1.GND
  N4: Raspberry_Pi_B_rev1.GPIO21, Part1.DO/RX
  N5: Raspberry_Pi_B_rev1.GPIO20, Part1.CK/TX
  N6: Raspberry_Pi_B_rev1.GPIO7, U1.NSS
  N7: Raspberry_Pi_B_rev1.GPIO8, U1.RST
  N8: Raspberry_Pi_B_rev1.GPIO23, Part1.GND

custom parts:
  RFID RC522 SIP - 8 pins: A SIP stand-in part for RFID RC522 . With 8 pins on a 300 mil single inline package (SIP) footprint.
